# Fritzing sketch Wiring_ESP32 (saved by Fritzing 0.9.10b)

parts:
  U1 = ESP32-38PinWide [part_number=ESP32-38PinWide]
  Bauteil1 = NRF24L01+ Breakout Board

nets:
  N1: U1.3.3, Bauteil1.VCC
  N2: U1.GPIO4, Bauteil1.CE
  N3: U1.GPIO16, Bauteil1.IRQ
  N4: U1.GPIO5, Bauteil1.CS
  N5: U1.GPIO18, Bauteil1.SCK
  N6: U1.GPIO19, Bauteil1.MISO
  GND: U1.GND, Bauteil1.GND
  N7: U1.GPIO23, Bauteil1.MOSI

custom parts:
  ESP32-38PinWide: Generic 38-Pin ESP32 with wide format (only access to one side of pins on a breadboard) based on Stephen Lilley's HiLetgo ESP-WROOM-32 ESP32 ESP-32S Development Board.
